# Fritzing sketch test (saved by Fritzing 0.9.3b)
breadboards: 1

parts:
  Part1 = Arduino Nano (Rev3.0)
  M1 = DC Motor
  Part3 = Thumb Joystick
  Part5 = Adafruit DRV8833 DC/Stepper Motor Driver [part_number="Adafruit #3297"]
  R1 = Resistor [tolerance=±5% resistance=47k package=THT]
  C1 = Electrolytic Capacitor [capacitance=10µF voltage=16V package="100 mil [THT, electrolytic]"]
  C2 = Capacitor [part_number=10nF package=cap-pth-small2]

nets:
  GND: Part1.GND, Part3.GND, Part5.GND, C1.-, C2.2
  N1: Part1.D2, Part3.SEL
  N2: Part1.D5, Part5.AIN1
  N3: Part1.D6, Part5.AIN2
  6V: Part1.VIN, Part5.VMOTOR, R1.Pin_0, C1.+, C2.1
  5V: Part1.5V, Part3.VCC
  N4: Part1.A1, Part3.VERT
  N5: Part1.A0, Part3.HORZ
  N6: M1.pin_1, Part5.AOUT1
  N7: M1.pin_2, Part5.AOUT2
  N8: Part5.!SLEEP, R1.Pin_1

notes:
  DRV8833 Test, 0.1

custom parts:
  Adafruit DRV8833 DC/Stepper Motor Driver: Spin two DC motors or step one bi-polar or uni-polar stepper with up to 1.2A per channel using the DRV8833. This motor driver chip is a nice alternative to the TB6612 driver. Like that chip, you get 2 full H-bridges, but this chip is better for low voltage uses (can run from 2.7V up to 10.8V motor power) and has built in current limiting capability. We set it up for 1A current limiting so you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
